# Fritzing sketch sketch (saved by Fritzing 0.9.4)
breadboards: 1

parts:
  Part1 = Arduino Nano (Rev3.0) (ICSP)
  U1 = POT [package=pot_alpha_rv16af-20]
  S1 = Pushbutton [package="[SMD]"]
  YwRobot_Power_Supply1 = YwRobot Breadboard Power Supply [part_number=545043]
  Mod1 = KY-019 5V Relay Module [package="Breakout board"]
  R1 = Resistor [tolerance=±5% resistance=10k package="0402 [SMD]"]
  J1 = Basic Servo  # not connected

nets (from the schematic view):
  N1: Part1.GND, YwRobot_Power_Supply1.GND#14, Mod1.-
  N2: Part1.D4, Mod1.S
  N3: Part1.D5, S1.Pin_3, S1.Pin_4, R1.Pin_1
  N4: Part1.VIN, YwRobot_Power_Supply1.VCC#10
  N5: Part1.A1, U1.S
  N6: U1.A, YwRobot_Power_Supply1.GND#12, R1.Pin_0
  N7: U1.E, YwRobot_Power_Supply1.VCC#9
  N8: S1.Pin_1, S1.Pin_2, YwRobot_Power_Supply1.VCC#5
  N9: YwRobot_Power_Supply1.VCC#6, Mod1.+

custom parts:
  YwRobot Breadboard Power Supply: The YwRobot Breadboard Power Supply (MB-V2) has two power rails; they can be 5V or 3V3. Power to the module can be provided through the female USB socket or through the A10 (female) 2.1mm power jack.
  KY-019 5V Relay Module: KY-019 5V Relay module, used to control AC circuits. (Special thanks to vanepp for fixing the PCB holes and other errors)
